// Logisim project Alarme.circ as structural Verilog: 1 circuit, main circuit main
module main (
  input  A,
  input  B,
  input  C
);

  wire and_1_out, or_1_out;

  or or_1 (or_1_out, A, B);
  and and_1 (and_1_out, or_1_out, C);
  LED S (.in(and_1_out));

  // Notes on the sheet:
  //   sensor porta
  //   sensor janela
  //   arma/desarma
  //   sirene
endmodule
