// Logisim project All Gates.circ as structural Verilog: 1 circuit, main circuit main
module main (
  input  A,
  input  A2,
  input  B2,
  input  B,
  input  C,
  input  C2,
  input  D2,
  input  D,
  input  E,
  input  C3,
  input  D3,
  input  A3,
  input  B3,
  output S1,
  output S4,
  output S2,
  output S5,
  output out_18,
  output S7,
  output S6
);

  not not_1 (S1, A);
  and and_1 (S2, B, C);
  or or_1 (out_18, D, E);
  xor xor_1 (S6, A3, B3);
  nand nand_1 (S4, A2, B2);
  nor nor_1 (S5, C2, D2);
  xnor xnor_1 (S7, C3, D3);

  // Notes on the sheet:
  //   PORTA NOT
  //   PORTA AND
  //   PORTA OR
  //   PORTA XOR
  //   PORTA NAND
  //   PORTA NOR
  //   PORTA XNOR
endmodule
