// Logisim project aula3.circ as structural Verilog: 1 circuit, main circuit main
module main (
  input  in_1,
  input  in_2,
  input  in_3,
  input  in_4,
  input  in_5,
  input  in_6,
  output out_7,
  output out_8,
  output out_9
);

  wire not_1_out, not_2_out, or_1_out, or_2_out, or_3_out;

  not not_1 (not_1_out, in_6);
  not not_2 (not_2_out, in_1);
  and and_1 (out_8, in_3, in_4);
  or or_1 (or_1_out, in_5, in_6);
  or or_2 (or_2_out, in_5, not_1_out);
  or or_3 (or_3_out, not_2_out, in_2);
  and and_2 (out_9, or_1_out, or_2_out);
  and and_3 (out_7, or_3_out, in_1);
endmodule
