// Logisim project demorgan.circ as structural Verilog: 1 circuit, main circuit main
module main (
  input  A,
  input  B,
  input  A_B___AB,
  input  in_4,
  output S,
  output out_6,
  output out_7,
  output out_8
);

  wire not_1_out, not_2_out, not_3_out, not_4_out;

  not not_1 (not_1_out, A);
  not not_2 (not_2_out, B);
  not not_3 (not_3_out, A_B___AB);
  not not_4 (not_4_out, in_4);
  nand nand_1 (S, A, B);
  nor nor_1 (out_7, A_B___AB, in_4);
  or or_1 (out_6, not_1_out, not_2_out);
  and and_1 (out_8, not_3_out, not_4_out);

  // Notes on the sheet:
  //   AB = A + B
  //   Teorema de Morgan
  //   AB = A+ B
endmodule
